# Fritzing sketch OliveTurtle 2 (saved by Fritzing 0.9.4)
circuit board: 8.46667cm x 5.64444cm
breadboards: 2

parts:
  MH-ET_LIVE_ESP32_DEVKIT1 = MH-ET LIVE ESP32 DEVKIT 38 pins
  12V_IN = Camdenboss CTB0158-2 [part_number=CTB0158-2 package=THT]
  Q1 = Basic FET N-Channel [part_number=IRF520 package="TO220 [THT]"]
  LED1 = Camdenboss CTB0158-2 [part_number=CTB0158-2 package=THT]
  U1 = TLP621 [package=THT]
  R1 = Resistor [tolerance=±5% resistance=330 package="0603 [SMD]"]
  R2 = Resistor [tolerance=±5% resistance=2.2k package="0603 [SMD]"]
  LED2 = Camdenboss CTB0158-2 [part_number=CTB0158-2 package=THT]
  Q2 = Basic FET N-Channel [part_number=IRF520 package="TO220 [THT]"]
  U2 = TLP621 [package=THT]
  R3 = Resistor [tolerance=±5% resistance=330 package="0603 [SMD]"]
  R4 = Resistor [tolerance=±5% resistance=2.2k package="0603 [SMD]"]

nets:
  N1: MH-ET_LIVE_ESP32_DEVKIT1.GND#70, U1.Pin_2, U2.Pin_2
  N2: MH-ET_LIVE_ESP32_DEVKIT1.IO17, R1.Pin_0
  N3: MH-ET_LIVE_ESP32_DEVKIT1.IO16, R3.Pin_0
  N4: 12V_IN.pin1, LED1.pin1, U1.Pin_3, LED2.pin1, U2.Pin_3
  N5: 12V_IN.pin2, Q1.drain, Q2.drain
  12V: 12V_IN.terminal_1
  GND: 12V_IN.terminal_2
  N6: Q1.gate, R2.Pin_1
  N7: Q1.source, LED1.pin2
  N8: U1.Pin_1, R1.Pin_1
  N9: U1.Pin_4, R2.Pin_0
  N10: LED2.pin2, Q2.source
  N11: Q2.gate, R4.Pin_1
  N12: U2.Pin_1, R3.Pin_1
  N13: U2.Pin_4, R4.Pin_0

custom parts:
  MH-ET LIVE ESP32 DEVKIT 38 pins: http://mh.nodebb.com/topic/2/mh-et-live-esp32-devkit
