# Fritzing sketch OliveTurtle (saved by Fritzing 0.9.4)
circuit board: 8.46667cm x 5.64444cm
breadboards: 2

parts:
  L2-PC = TLP621 [package=THT]
  L1-PC = TLP621 [package=THT]
  L1-R2 = Resistor [tolerance=±5% resistance=2.2k package="0603 [SMD]"]
  L2-R2 = Resistor [tolerance=±5% resistance=2.2k package="0603 [SMD]"]
  L2-R1 = Resistor [tolerance=±5% resistance=330 package="0603 [SMD]"]
  L2-T = Basic FET N-Channel [part_number=IRF520 package="TO220 [THT]"]
  L1-R1 = Resistor [tolerance=±5% resistance=330 package="0603 [SMD]"]
  L1-T = Basic FET N-Channel [part_number=IRF520 package="TO220 [THT]"]
  MH-ET_LIVE_ESP32_DEVKIT1 = MH-ET LIVE ESP32 DEVKIT 38 pins
  L2 = Camdenboss CTB0158-2 [part_number=CTB0158-2 package=THT]
  L1 = Camdenboss CTB0158-2 [part_number=CTB0158-2 package=THT]
  L-IN_12V = Camdenboss CTB0158-2 [part_number=CTB0158-2 package=THT]

nets:
  N1: L2-PC.Pin_1, L2-R1.Pin_1
  N2: L2-PC.Pin_2, L1-PC.Pin_2, MH-ET_LIVE_ESP32_DEVKIT1.GND#70
  N3: L2-PC.Pin_4, L1-PC.Pin_4, L2.pin1, L1.pin1, L-IN_12V.pin1
  N4: L2-PC.Pin_3, L2-R2.Pin_0
  N5: L1-PC.Pin_1, L1-R1.Pin_1
  N6: L1-PC.Pin_3, L1-R2.Pin_0, L1-T.gate
  N7: L1-R2.Pin_1, L2-T.source, L1-T.source, L-IN_12V.pin2
  N8: L2-R2.Pin_1, L2-T.gate
  N9: L2-R1.Pin_0, MH-ET_LIVE_ESP32_DEVKIT1.IO17
  N10: L2-T.drain, L2.pin2
  N11: L1-R1.Pin_0, MH-ET_LIVE_ESP32_DEVKIT1.IO22
  N12: L1-T.drain, L1.pin2

custom parts:
  MH-ET LIVE ESP32 DEVKIT 38 pins: http://mh.nodebb.com/topic/2/mh-et-live-esp32-devkit
